# Fritzing sketch Proy (saved by Fritzing 0.9.3b)
circuit board: 8.46667cm x 5.64444cm
breadboards: 1

parts:
  Arduino_1 = Arduino Uno (Rev3)
  R1 = Photocell (LDR) [package=THT]
  R2 = Resistor [tolerance=±5% resistance=220 package=THT]
  Sensor_Temp/Hum_1 = Humidity and Temperature Sensor RHT03
  Receiver_RF = Grove Infrared Receiver
  Emitter_RF = Grove Infrared Emitter
  RTC_1 = Real Time Clock Module - DS1307 RTC Breakout Board
  LCM1602_IIC2 = LCM1602 IIC [part_number="I2C 1" chip_label="bus I2C" package="DIP (Dual Inline) [THT]"]
  LCD1 = LCD screen
  Sensor_Pluja_1 = Soil Moisture Sensor
  R3 = Resistor [tolerance=±5% resistance=10k package=THT]

nets:
  N1: Arduino_1.A0, R1.pin_0, R2.Pin_0
  N2: Arduino_1.A4/SDA, RTC_1.SDA, LCM1602_IIC2.SDA
  N3: Arduino_1.A5/SCL, RTC_1.SCL, LCM1602_IIC2.SCL
  N4: Arduino_1.D8, Sensor_Temp/Hum_1.Data-signal
  N5: Arduino_1.D9_PWM, Emitter_RF.TX
  N6: Arduino_1.D10_PWM/SS, Sensor_Pluja_1.SIG
  N7: Arduino_1.D2, Receiver_RF.RX, R3.Pin_1
  VCC: Arduino_1.5V, Sensor_Temp/Hum_1.Vcc, Receiver_RF.VCC, Emitter_RF.VCC, RTC_1.5V, LCM1602_IIC2.VCC
  GND: Arduino_1.GND, R1.pin_1, Sensor_Temp/Hum_1.GND_2, Receiver_RF.GND, Emitter_RF.GND, RTC_1.GND, LCM1602_IIC2.GND, Sensor_Pluja_1.GND, R3.Pin_0
  N8: R2.Pin_1, Sensor_Pluja_1.VCC
  VSS: LCM1602_IIC2.VSS, LCD1.VSS
  VDD: LCM1602_IIC2.VDD, LCD1.VDD
  N9: LCM1602_IIC2.V0, LCD1.V0
  N10: LCM1602_IIC2.RS, LCD1.RS
  N11: LCM1602_IIC2.RW, LCD1.R/W
  N12: LCM1602_IIC2.E, LCD1.E
  N13: LCM1602_IIC2.D0, LCD1.DB0
  N14: LCM1602_IIC2.D1, LCD1.DB1
  N15: LCM1602_IIC2.D2, LCD1.DB2
  N16: LCM1602_IIC2.D3, LCD1.DB3
  N17: LCM1602_IIC2.D4, LCD1.DB4
  N18: LCM1602_IIC2.D5, LCD1.DB5
  N19: LCM1602_IIC2.D6, LCD1.DB6
  N20: LCM1602_IIC2.D7, LCD1.DB7
  N21: LCM1602_IIC2.A, LCD1.LED+
  N22: LCM1602_IIC2.K, LCD1.LED-
  N23: LCM1602_IIC2.LED_A, LCM1602_IIC2.LED_B

custom parts:
  LCM1602 IIC: I2C-Module to use a 1602 or 2004 LCD on with the wire.h libory Serial LCD Modul
